// Logisim project cpu.circ as structural Verilog: 1 circuit, main circuit cpu
module cpu (
  input  clk,
  input  [31:0] INSTRUCTION,
  input  [31:0] READ_DATA,
  output [31:0] WRITE_ADDRESS,
  output [31:0] PROGRAM_COUNTER,
  output [31:0] ra,
  output [31:0] sp,
  output [31:0] t0,
  output [31:0] t1,
  output [31:0] t2,
  output [31:0] s0,
  output [31:0] s1,
  output [31:0] a0,
  output [31:0] tohost,
  output [3:0] WRITE_ENABLE,
  output [31:0] WRITE_DATA
);

  wire ASel, BSel, REGWEn;
  wire [1:0] WBSel;
  wire [2:0] ImmSel;
  wire [3:0] ALUSel;
  wire [31:0] A_OUT, adder_1_out, ALU_OUT, B_OUT, IF_ID_INSTR, IF_ID_PC, IMM_OUT, RS1_OUT, RS2_OUT, WB;

  Adder #(.width(32)) adder_1 (.a(PROGRAM_COUNTER), .b(32'h4), .out(adder_1_out));  // open: cin, cout
  Register #(.width(32)) PC (.D(adder_1_out), .clk(clk), .Q(PROGRAM_COUNTER));  // open: en, clr
  Register #(.width(32)) IF_ID_1 (.D(INSTRUCTION), .clk(clk), .Q(IF_ID_INSTR));  // open: en, clr
  Register #(.width(32)) IF_ID_2 (.D(PROGRAM_COUNTER), .clk(clk), .Q(IF_ID_PC));  // open: en, clr
  control_logic control_logic_1 (
    .RegWEn(REGWEn), .ImmSel(ImmSel), .ASel(ASel), .BSel(BSel), .ALUSel(ALUSel), .WBSel(WBSel),
    .inst(IF_ID_INSTR));  // open: CSRWen, PCSel, BrUn, MemRW, CSRSel, BrEq, BrLt
  imm_gen imm_gen_1 (.inst(IF_ID_INSTR), .ImmSel(ImmSel), .imm(IMM_OUT));
  Multiplexer #(.enable("false"), .width(32)) multiplexer_1 (
    .in0(RS1_OUT), .in1(PROGRAM_COUNTER), .out(A_OUT), .sel(ASel));
  Multiplexer #(.enable("false"), .width(32)) multiplexer_2 (.in0(RS2_OUT), .in1(IMM_OUT), .out(B_OUT), .sel(BSel));
  regfile regfile_1 (
    .rs1(IF_ID_INSTR[19:15]), .rs2(IF_ID_INSTR[24:20]), .rd(IF_ID_INSTR[11:7]), .Write_Data(WB),
    .RegWEn(REGWEn), .clk(clk), .ra(ra), .sp(sp), .t0(t0), .t1(t1), .t2(t2), .s0(s0), .s1(s1), .a0(a0),
    .Read_Data_1(RS1_OUT), .Read_Data_2(RS2_OUT));
  // branch_comp branch_comp_1: pin names not known
  Multiplexer #(.enable("false"), .select(2), .width(32)) multiplexer_3 (
    .in1(ALU_OUT), .out(WB), .sel(WBSel));  // open: in0, in2, in3
  alu alu_1 (.Result(ALU_OUT), .A(A_OUT), .B(B_OUT), .ALUSel(ALUSel));
  csr csr_1 (.tohost(tohost));  // open: CSR_address, CSR_din, CSR_WE, clk

  // Notes on the sheet:
  //   Output to IMEM
  //   IMEM (do **NOT** move this)
  //   Inputs from IMEM
  //   It is OK to move the PC, RegFile, ALU, MEM, Branch Comp, Imm Gen, and Control Logic to wherever is most convenient for you when constructing your CPU, and to delete this text
  //   Inputs/Outputs for testing. Do **NOT** move these.
  //   Outputs To DMEM
  //   DMEM (do **NOT** move this)
  //   Inputs From DMEM
endmodule
