// Logisim project branch_comp.circ as structural Verilog: 1 circuit, main circuit branch_comp
module branch_comp (
  input  [31:0] rs1,
  input  [31:0] rs2,
  input  BrUn,
  output BrEq,
  output BrLt
);

  wire subtractor_1_bout;
  wire [31:0] bit_extender_1_out, multiplexer_1_out, subtractor_1_out;

  Subtractor #(.width(32)) subtractor_1 (
    .a(rs1), .b(rs2), .out(subtractor_1_out), .bout(subtractor_1_bout));  // open: bin
  assign bit_extender_1_out = {{31{subtractor_1_bout}}, subtractor_1_bout};  // Bit_Extender bit_extender_1
  Comparator #(.width(32)) comparator_1 (.a(subtractor_1_out), .b({32{1'b0}}), .eq(BrEq));  // open: gt, lt
  Multiplexer #(.enable("false"), .width(32)) multiplexer_1 (
    .in0(subtractor_1_out), .in1(bit_extender_1_out), .out(multiplexer_1_out), .sel(BrUn));
  Comparator #(.width(32)) comparator_2 (.a(multiplexer_1_out), .b({32{1'b0}}), .lt(BrLt));  // open: gt, eq

  // Notes on the sheet:
  //   INPUTS to your circuit
  //   DON'T CHANGE THE LOCATIONS OF THE INPUTS AND OUTPUTS!
  //   OUTPUT from your circuit
endmodule
