// Logisim project control_logic.circ as structural Verilog: 1 circuit, main circuit control_logic
module control_logic (
  input  [31:0] inst,
  input  BrEq,
  input  BrLt,
  output PCSel,
  output RegWEn,
  output [2:0] ImmSel,
  output BrUn,
  output ASel,
  output BSel,
  output [3:0] ALUSel,
  output MemRW,
  output [1:0] WBSel,
  output CSRSel,
  output CSRWen
);

  wire and_2_out, and_3_out, and_4_out, and_5_out, and_6_out, and_7_out, comparator_1_eq, comparator_2_eq,
       CSRSel1, multiplexer_4_out, not_1_out, not_2_out, not_3_out, not_4_out, not_5_out, not_6_out,
       not_7_out, not_8_out, not_9_out, not_10_out, not_11_out, or_1_out, or_2_out, PC_Sel_1;
  wire [1:0] ALU_1;
  wire [3:0] ITypeALUDecode_data, multiplexer_1_out, multiplexer_2_out, multiplexer_3_out,
       RTypeALUDecode_data;

  ROM #(.addrWidth(3), .dataWidth(4)) ITypeALUDecode (.addr(inst[14:12]), .data(ITypeALUDecode_data));
  ROM #(.addrWidth(10), .dataWidth(4)) RTypeALUDecode (.addr({inst[14:12], inst[31:25]}), .data(RTypeALUDecode_data));
  ROM #(.addrWidth(7), .dataWidth(14)) rom_1 (
    .addr(inst[6:0]), .data({PC_Sel_1, RegWEn, ImmSel, ASel, BSel, ALU_1, MemRW, WBSel, CSRSel1, CSRWen}));
  and and_1 (BrUn, inst[13], inst[14]);
  not not_1 (not_1_out, BrEq);
  Comparator #(.width(7)) comparator_1 (.a(7'b0110111), .b(inst[6:0]), .eq(comparator_1_eq));  // open: gt, lt
  not not_2 (not_2_out, ITypeALUDecode_data[0]);
  not not_3 (not_3_out, ITypeALUDecode_data[1]);
  not not_4 (not_4_out, ITypeALUDecode_data[3]);
  not not_5 (not_5_out, BrEq);
  not not_6 (not_6_out, BrUn);
  not not_7 (not_7_out, BrUn);
  not not_8 (not_8_out, BrLt);
  not not_9 (not_9_out, BrUn);
  not not_10 (not_10_out, BrEq);
  not not_11 (not_11_out, BrLt);
  Multiplexer #(.enable("false"), .width(4)) multiplexer_1 (
    .in0(4'b1100), .in1(4'b1101), .out(multiplexer_1_out), .sel(or_1_out));
  or or_1 (or_1_out, comparator_1_eq, comparator_2_eq);
  Comparator #(.width(7)) comparator_2 (.a(7'b0010111), .b(inst[6:0]), .eq(comparator_2_eq));  // open: gt, lt
  Multiplexer #(.enable("false"), .width(4)) multiplexer_2 (
    .in0(4'b0100), .in1(4'b0101), .out(multiplexer_2_out), .sel(inst[30]));
  and and_2 (and_2_out, not_2_out, not_3_out, ITypeALUDecode_data[2], not_4_out);
  and and_3 (and_3_out, not_5_out, not_6_out);
  and and_4 (and_4_out, BrLt, not_1_out, not_7_out);
  and and_5 (and_5_out, not_8_out, not_9_out);
  and and_6 (and_6_out, BrLt, BrUn, not_10_out);
  and and_7 (and_7_out, not_11_out, BrUn);
  Multiplexer #(.enable("false"), .width(4)) multiplexer_3 (
    .in0(ITypeALUDecode_data), .in1(multiplexer_2_out), .out(multiplexer_3_out), .sel(and_2_out));
  Multiplexer #(.enable("false"), .select(3)) multiplexer_4 (
    .in0(BrEq), .in1(and_3_out), .in4(and_4_out), .in5(and_5_out), .in6(and_6_out), .in7(and_7_out),
    .out(multiplexer_4_out), .sel(inst[14:12]));  // open: in2, in3
  Multiplexer #(.enable("false"), .select(2), .width(4)) multiplexer_5 (
    .in0(4'b0000), .in1(RTypeALUDecode_data), .in2(multiplexer_1_out), .in3(multiplexer_3_out), .out(ALUSel),
    .sel(ALU_1));
  or or_2 (or_2_out, inst[2], multiplexer_4_out);
  and and_8 (PCSel, PC_Sel_1, or_2_out);
  and and_9 (CSRSel, inst[14], CSRSel1);

  // Other names for the same wires on the sheet: func7[6:0] = inst[31:25]; sign = inst[30]; func3[2:0] = inst[14:12];
  //   opcode[6:0] = inst[6:0]

  // Notes on the sheet:
  //   contents of ITypeALUDecode (hex, n*v repeats v):
  //   0 6 7 0 3 4 2 1
  //   INPUTS to your circuit
  //   contents of RTypeALUDecode (hex, n*v repeats v):
  //   0 a 30*0 c 95*0 6 e 126*0 7 128*0 b 126*0 3 127*0 4 31*0 5 95*0 2 127*0 1
  //   contents of rom_1 (hex, n*v repeats v):
  //   0 0 0 1280 15*0 12e4 0 0 0 18c4 11*0 490 15*0 1024 0 0 0 19c4 43*0 2780 0 0 0 3288 7*0 3b88 0 0 0
  //   1e8f
  //   DON'T CHANGE THE LOCATIONS OF THE INPUTS AND OUTPUTS!
  //   OUTPUT from your circuit
endmodule
