// Logisim project cpu.circ as structural Verilog: 2 circuits, main circuit cpu
module cpu (
  input  clk,
  input  [31:0] INSTRUCTION,
  input  [31:0] READ_DATA,
  output [31:0] WRITE_ADDRESS,
  output [31:0] PROGRAM_COUNTER,
  output [31:0] ra,
  output [31:0] sp,
  output [31:0] t0,
  output [31:0] t1,
  output [31:0] t2,
  output [31:0] s0,
  output [31:0] s1,
  output [31:0] a0,
  output [31:0] tohost,
  output [3:0] WRITE_ENABLE,
  output [31:0] WRITE_DATA
);

  wire ASel, BrEq, BrLt, BrUn, BSel, comparator_1_eq, CSRSel, CSRWen, EX_MEM_REGWEn, ID_EX_ASel, ID_EX_BSel,
       ID_EX_REGWEn, MemRW, multiplexer_4_out, PCSel, REGWEn, WB_REGWEn;
  wire [1:0] EX_MEM_WBSel, FORWARD_A, FORWARD_B, ID_EX_WBSel, WBSel;
  wire [2:0] ID_EX_ImmSel, ImmSel;
  wire [3:0] ALUSel, ID_EX_ALUSel, rom_1_data;
  wire [4:0] ACTUAL_RS1, EX_MEM_RD, ID_EX_RD, ID_EX_Reg1, ID_EX_Reg2, WB_RD;
  wire [31:0] A_OUT, B_OUT, EX_MEM_ALU, EX_MEM_PC, EX_MEM_RS2, ID_EX_IMM, ID_EX_PC, ID_EX_RS1, ID_EX_RS2,
       IF_ID_INSTR, IF_ID_NEXT_PC, IF_ID_PC, IMM_OUT, multiplexer_1_out, multiplexer_3_out, NEXT_PC, RS1_OUT,
       WB, WB_WB;

  Adder #(.width(32)) adder_1 (.a(PROGRAM_COUNTER), .b(32'h4), .out(NEXT_PC));  // open: cin, cout
  Register #(.width(32)) PC (.D(multiplexer_1_out), .clk(clk), .Q(PROGRAM_COUNTER));  // open: en, clr
  Multiplexer #(.enable("false"), .width(32)) multiplexer_1 (
    .in0(NEXT_PC), .in1(WRITE_ADDRESS), .out(multiplexer_1_out), .sel(PCSel));
  Multiplexer #(.enable("false"), .width(5)) multiplexer_2 (
    .in0(IF_ID_INSTR[19:15]), .in1({5{1'b0}}), .out(ACTUAL_RS1), .sel(CSRSel));
  Register #(.width(32)) IF_ID_1 (.D(multiplexer_3_out), .clk(clk), .Q(IF_ID_INSTR));  // open: en, clr
  Multiplexer #(.enable("false"), .width(32)) multiplexer_3 (
    .in0(INSTRUCTION), .in1({32{1'b0}}), .out(multiplexer_3_out), .sel(PCSel));
  Register #(.width(32)) IF_ID_2 (.D(PROGRAM_COUNTER), .clk(clk), .Q(IF_ID_PC));  // open: en, clr
  Register #(.width(32)) register_1 (.D(NEXT_PC), .clk(clk), .Q(IF_ID_NEXT_PC));  // open: en, clr
  Comparator #(.width(5)) comparator_1 (.a(IF_ID_INSTR[11:7]), .b({5{1'b0}}), .eq(comparator_1_eq));  // open: gt, lt
  Multiplexer #(.enable("false")) multiplexer_4 (
    .in0(REGWEn), .in1(1'b0), .out(multiplexer_4_out), .sel(comparator_1_eq));
  imm_gen imm_gen_1 (.inst(IF_ID_INSTR), .ImmSel(ImmSel), .imm(IMM_OUT));
  Multiplexer #(.enable("false"), .select(2), .width(32)) multiplexer_5 (
    .in1(WRITE_ADDRESS), .in3(WB), .sel(FORWARD_A));  // open: in0, in2, out
  Multiplexer #(.enable("false"), .select(2), .width(32)) multiplexer_6 (
    .in1(EX_MEM_ALU), .in3(WB), .sel(FORWARD_B));  // open: in0, in2, out
  control_logic control_logic_1 (
    .CSRWen(CSRWen), .PCSel(PCSel), .RegWEn(REGWEn), .ImmSel(ImmSel), .BrUn(BrUn), .ASel(ASel), .BSel(BSel),
    .ALUSel(ALUSel), .MemRW(MemRW), .WBSel(WBSel), .CSRSel(CSRSel), .inst(IF_ID_INSTR), .BrEq(BrEq),
    .BrLt(BrLt));
  Register #(.width(32)) ID_EX_1 (.D(IF_ID_PC), .clk(clk), .Q(ID_EX_PC));  // open: en, clr
  Register #(.width(32)) ID_EX_2 (.D(IMM_OUT), .clk(clk), .Q(ID_EX_IMM));  // open: en, clr
  Register #(.width(32)) ID_EX_3 (.D(RS1_OUT), .clk(clk), .Q(ID_EX_RS1));  // open: en, clr
  Register #(.width(32)) ID_EX_4 (.D(WRITE_DATA), .clk(clk), .Q(ID_EX_RS2));  // open: en, clr
  Register #(.width(1)) register_2 (.D(REGWEn), .clk(clk), .Q(ID_EX_REGWEn));  // open: en, clr
  Register #(.width(3)) register_3 (.D(ImmSel), .clk(clk), .Q(ID_EX_ImmSel));  // open: en, clr
  Register #(.width(1)) register_4 (.D(ASel), .clk(clk), .Q(ID_EX_ASel));  // open: en, clr
  Register #(.width(1)) register_5 (.D(BSel), .clk(clk), .Q(ID_EX_BSel));  // open: en, clr
  Register #(.width(4)) register_6 (.D(ALUSel), .clk(clk), .Q(ID_EX_ALUSel));  // open: en, clr
  Register #(.width(2)) register_7 (.D(WBSel), .clk(clk), .Q(ID_EX_WBSel));  // open: en, clr
  Register #(.width(5)) register_8 (.D(IF_ID_INSTR[11:7]), .clk(clk), .Q(ID_EX_RD));  // open: en, clr
  Register #(.width(5)) register_9 (.D(IF_ID_INSTR[19:15]), .clk(clk), .Q(ID_EX_Reg1));  // open: en, clr
  Register #(.width(5)) register_10 (.D(IF_ID_INSTR[24:20]), .clk(clk), .Q(ID_EX_Reg2));  // open: en, clr
  Multiplexer #(.enable("false"), .width(32)) multiplexer_7 (.in0(RS1_OUT), .in1(IF_ID_PC), .out(A_OUT), .sel(ASel));
  Multiplexer #(.enable("false"), .width(32)) multiplexer_8 (.in0(WRITE_DATA), .in1(IMM_OUT), .out(B_OUT), .sel(BSel));
  forward forward_1 (
    .RS1(ID_EX_Reg1), .EXMEM_RD(EX_MEM_RD), .MEMWB_RD(WB_RD), .RS2(ID_EX_Reg2), .ForwardA(FORWARD_A),
    .ForwardB(FORWARD_B));
  regfile regfile_1 (
    .rs1(ACTUAL_RS1), .rs2(IF_ID_INSTR[24:20]), .rd(IF_ID_INSTR[11:7]), .Write_Data(WB),
    .RegWEn(multiplexer_4_out), .clk(clk), .ra(ra), .sp(sp), .t0(t0), .t1(t1), .t2(t2), .s0(s0), .s1(s1),
    .a0(a0), .Read_Data_1(RS1_OUT), .Read_Data_2(WRITE_DATA));
  branch_comp branch_comp_1 (.rs1(RS1_OUT), .rs2(WRITE_DATA), .BrUn(BrUn), .BrEq(BrEq), .BrLt(BrLt));
  Register #(.width(32)) EX_MEM_1 (.D(ID_EX_PC), .clk(clk), .Q(EX_MEM_PC));  // open: en, clr
  Register #(.width(32)) EX_MEM_2 (.D(WRITE_ADDRESS), .clk(clk), .Q(EX_MEM_ALU));  // open: en, clr
  Register #(.width(32)) EX_MEM_3 (.D(ID_EX_RS2), .clk(clk), .Q(EX_MEM_RS2));  // open: en, clr
  Register #(.width(2)) register_11 (.D(ID_EX_WBSel), .clk(clk), .Q(EX_MEM_WBSel));  // open: en, clr
  Register #(.width(5)) register_12 (.D(ID_EX_RD), .clk(clk), .Q(EX_MEM_RD));  // open: en, clr
  Register #(.width(1)) register_13 (.D(ID_EX_REGWEn), .clk(clk), .Q(EX_MEM_REGWEn));  // open: en, clr
  Multiplexer #(.enable("false"), .select(2), .width(32)) multiplexer_9 (
    .in0(READ_DATA), .in1(WRITE_ADDRESS), .in2(IF_ID_NEXT_PC), .out(WB), .sel(WBSel));  // open: in3
  Register #(.width(32)) register_14 (.D(WB), .clk(clk), .Q(WB_WB));  // open: en, clr
  Register #(.width(5)) register_15 (.D(EX_MEM_RD), .clk(clk), .Q(WB_RD));  // open: en, clr
  Register #(.width(1)) register_16 (.D(EX_MEM_REGWEn), .clk(clk), .Q(WB_REGWEn));  // open: en, clr
  alu alu_1 (.Result(WRITE_ADDRESS), .A(A_OUT), .B(B_OUT), .ALUSel(ALUSel));
  ROM #(.addrWidth(3), .dataWidth(4)) rom_1 (.addr(IF_ID_INSTR[14:12]), .data(rom_1_data));
  Multiplexer #(.enable("false"), .width(4)) multiplexer_10 (
    .in0(4'b0000), .in1(rom_1_data), .out(WRITE_ENABLE), .sel(MemRW));
  csr csr_1 (.CSR_din(WRITE_ADDRESS), .CSR_WE(CSRWen), .clk(clk), .tohost(tohost));  // open: CSR_address

  // Other names for the same wires on the sheet: ALU_OUT[31:0] = WRITE_ADDRESS; IF_ID_RD[4:0] = IF_ID_INSTR[11:7];
  //   IF_ID_RS1[4:0] = IF_ID_INSTR[19:15]; IF_ID_RS2[4:0] = IF_ID_INSTR[24:20]; RS2_OUT[31:0] = WRITE_DATA

  // Notes on the sheet:
  //   Output to IMEM
  //   IMEM (do **NOT** move this)
  //   Inputs from IMEM
  //   It is OK to move the PC, RegFile, ALU, MEM, Branch Comp, Imm Gen, and Control Logic to wherever is most convenient for you when constructing your CPU, and to delete this text
  //   Inputs/Outputs for testing. Do **NOT** move these.
  //   contents of rom_1 (hex, n*v repeats v):
  //   1 3 f
  //   Outputs To DMEM
  //   DMEM (do **NOT** move this)
  //   Inputs From DMEM
endmodule

module forward (
  input  [4:0] RS1,
  input  [4:0] EXMEM_RD,
  input  [4:0] MEMWB_RD,
  input  [4:0] RS2,
  output [1:0] ForwardA,
  output [1:0] ForwardB
);

  wire comparator_1_eq, comparator_2_eq, comparator_3_eq, comparator_4_eq;
  wire [1:0] bit_extender_1_out, bit_extender_2_out, bit_extender_3_out, bit_extender_4_out;

  Comparator #(.width(5)) comparator_1 (.a(RS1), .b(EXMEM_RD), .eq(comparator_1_eq));  // open: gt, lt
  Comparator #(.width(5)) comparator_2 (.a(RS1), .b(MEMWB_RD), .eq(comparator_2_eq));  // open: gt, lt
  Comparator #(.width(5)) comparator_3 (.a(EXMEM_RD), .b(RS2), .eq(comparator_3_eq));  // open: gt, lt
  Comparator #(.width(5)) comparator_4 (.a(MEMWB_RD), .b(RS2), .eq(comparator_4_eq));  // open: gt, lt
  assign bit_extender_1_out = {{1{1'b0}}, comparator_1_eq};  // Bit_Extender bit_extender_1
  assign bit_extender_2_out = {{1{comparator_2_eq}}, comparator_2_eq};  // Bit_Extender bit_extender_2
  assign bit_extender_3_out = {{1{1'b0}}, comparator_3_eq};  // Bit_Extender bit_extender_3
  assign bit_extender_4_out = {{1{comparator_4_eq}}, comparator_4_eq};  // Bit_Extender bit_extender_4
  Multiplexer #(.enable("false"), .width(2)) multiplexer_1 (
    .in0(bit_extender_4_out), .in1(bit_extender_3_out), .out(ForwardB), .sel(comparator_3_eq));
  Multiplexer #(.enable("false"), .width(2)) multiplexer_2 (
    .in0(bit_extender_2_out), .in1(bit_extender_1_out), .out(ForwardA), .sel(comparator_1_eq));
endmodule
