// Logisim project imm_gen.circ as structural Verilog: 1 circuit, main circuit imm_gen
module imm_gen (
  input  [31:0] inst,
  input  [2:0] ImmSel,
  output [31:0] imm
);

  wire [31:0] bit_extender_1_out, csr_type, i_type, s_type, sb_type, uj_type;

  assign bit_extender_1_out = {{27{1'b0}}, inst[19:15]};  // Bit_Extender bit_extender_1
  assign i_type = {{20{inst[31]}}, inst[31:20]};  // Bit_Extender bit_extender_2
  assign s_type = {{20{inst[31]}}, {inst[31:25], inst[11:7]}};  // Bit_Extender bit_extender_3
  Multiplexer #(.enable("false"), .width(32)) multiplexer_1 (
    .in0({32{1'b0}}), .in1(bit_extender_1_out), .out(csr_type), .sel(inst[14]));
  assign sb_type = {{19{inst[31]}}, {inst[31], inst[7], inst[30:25], inst[11:8], 1'b0}};  // Bit_Extender bit_extender_4
  assign uj_type = {{11{inst[31]}}, {inst[31], inst[19:12], inst[20], inst[30:21], 1'b0}};  // Bit_Extender bit_extender_5
  Multiplexer #(.enable("false"), .select(3), .width(32)) multiplexer_2 (
    .in1(i_type), .in2(s_type), .in3(sb_type), .in4({inst[31:12], {12{1'b0}}}), .in5(uj_type),
    .in7(csr_type), .out(imm), .sel(ImmSel));  // open: in0, in6

  // Other names for the same wires on the sheet: u_type[31:12] = inst[31:12]

  // Notes on the sheet:
  //   INPUTS to your circuit
  //   DON'T CHANGE THE LOCATIONS OF THE INPUTS AND OUTPUTS!
  //   OUTPUT from your circuit
endmodule
