// Logisim project regfile.circ as structural Verilog: 2 circuits, main circuit regfile
module regfile (
  input  [4:0] rs1,
  input  [4:0] rs2,
  input  [4:0] rd,
  input  [31:0] Write_Data,
  input  RegWEn,
  input  clk,
  output [31:0] ra,
  output [31:0] sp,
  output [31:0] t0,
  output [31:0] t1,
  output [31:0] t2,
  output [31:0] s0,
  output [31:0] s1,
  output [31:0] a0,
  output [31:0] Read_Data_1,
  output [31:0] Read_Data_2
);

  wire regdatainput_1_writeflag, regdatainput_2_writeflag, regdatainput_3_writeflag,
       regdatainput_4_writeflag, regdatainput_5_writeflag, regdatainput_6_writeflag,
       regdatainput_7_writeflag, regdatainput_8_writeflag, regdatainput_9_writeflag,
       regdatainput_10_writeflag, regdatainput_11_writeflag, regdatainput_12_writeflag,
       regdatainput_13_writeflag, regdatainput_14_writeflag, regdatainput_15_writeflag,
       regdatainput_16_writeflag, regdatainput_17_writeflag, regdatainput_18_writeflag,
       regdatainput_19_writeflag, regdatainput_20_writeflag, regdatainput_21_writeflag,
       regdatainput_22_writeflag, regdatainput_23_writeflag, regdatainput_24_writeflag,
       regdatainput_25_writeflag, regdatainput_26_writeflag, regdatainput_27_writeflag,
       regdatainput_28_writeflag, regdatainput_29_writeflag, regdatainput_30_writeflag,
       regdatainput_31_writeflag;
  wire [31:0] inx1, inx2, inx3, inx4, inx5, inx6, inx7, inx8, inx9, inx10, inx11, inx12, inx13, inx14, inx15,
       inx16, inx17, inx18, inx19, inx20, inx21, inx22, inx23, inx24, inx25, inx26, inx27, inx28, inx29,
       inx30, inx31, outx0, outx3, outx4, outx11, outx12, outx13, outx14, outx15, outx16, outx17, outx18,
       outx19, outx20, outx21, outx22, outx23, outx24, outx25, outx26, outx27, outx28, outx29, outx30,
       outx31, regdatainput_1_data_out, regdatainput_2_data_out, regdatainput_3_data_out,
       regdatainput_4_data_out, regdatainput_5_data_out, regdatainput_6_data_out, regdatainput_7_data_out,
       regdatainput_8_data_out, regdatainput_9_data_out, regdatainput_10_data_out, regdatainput_11_data_out,
       regdatainput_12_data_out, regdatainput_13_data_out, regdatainput_14_data_out,
       regdatainput_15_data_out, regdatainput_16_data_out, regdatainput_17_data_out,
       regdatainput_18_data_out, regdatainput_19_data_out, regdatainput_20_data_out,
       regdatainput_21_data_out, regdatainput_22_data_out, regdatainput_23_data_out,
       regdatainput_24_data_out, regdatainput_25_data_out, regdatainput_26_data_out,
       regdatainput_27_data_out, regdatainput_28_data_out, regdatainput_29_data_out,
       regdatainput_30_data_out, regdatainput_31_data_out;

  Register #(.width(32)) x0 (.D({32{1'b0}}), .clk(clk), .Q(outx0));  // open: en, clr
  Register #(.width(32)) x1 (
    .D(regdatainput_1_data_out), .en(regdatainput_1_writeflag), .clk(clk), .Q(ra));  // open: clr
  regdatainput regdatainput_1 (
    .data_in(inx1), .write_en(RegWEn), .data_out(regdatainput_1_data_out),
    .writeflag(regdatainput_1_writeflag));
  Register #(.width(32)) x2 (
    .D(regdatainput_2_data_out), .en(regdatainput_2_writeflag), .clk(clk), .Q(sp));  // open: clr
  regdatainput regdatainput_2 (
    .data_in(inx2), .write_en(RegWEn), .data_out(regdatainput_2_data_out),
    .writeflag(regdatainput_2_writeflag));
  Register #(.width(32)) x3 (
    .D(regdatainput_3_data_out), .en(regdatainput_3_writeflag), .clk(clk), .Q(outx3));  // open: clr
  regdatainput regdatainput_3 (
    .data_in(inx3), .write_en(RegWEn), .data_out(regdatainput_3_data_out),
    .writeflag(regdatainput_3_writeflag));
  Register #(.width(32)) x4 (
    .D(regdatainput_4_data_out), .en(regdatainput_4_writeflag), .clk(clk), .Q(outx4));  // open: clr
  regdatainput regdatainput_4 (
    .data_in(inx4), .write_en(RegWEn), .data_out(regdatainput_4_data_out),
    .writeflag(regdatainput_4_writeflag));
  Register #(.width(32)) x5 (
    .D(regdatainput_5_data_out), .en(regdatainput_5_writeflag), .clk(clk), .Q(t0));  // open: clr
  regdatainput regdatainput_5 (
    .data_in(inx5), .write_en(RegWEn), .data_out(regdatainput_5_data_out),
    .writeflag(regdatainput_5_writeflag));
  Register #(.width(32)) x6 (
    .D(regdatainput_6_data_out), .en(regdatainput_6_writeflag), .clk(clk), .Q(t1));  // open: clr
  regdatainput regdatainput_6 (
    .data_in(inx6), .write_en(RegWEn), .data_out(regdatainput_6_data_out),
    .writeflag(regdatainput_6_writeflag));
  Register #(.width(32)) x7 (
    .D(regdatainput_7_data_out), .en(regdatainput_7_writeflag), .clk(clk), .Q(t2));  // open: clr
  regdatainput regdatainput_7 (
    .data_in(inx7), .write_en(RegWEn), .data_out(regdatainput_7_data_out),
    .writeflag(regdatainput_7_writeflag));
  Register #(.width(32)) x8 (
    .D(regdatainput_8_data_out), .en(regdatainput_8_writeflag), .clk(clk), .Q(s0));  // open: clr
  regdatainput regdatainput_8 (
    .data_in(inx8), .write_en(RegWEn), .data_out(regdatainput_8_data_out),
    .writeflag(regdatainput_8_writeflag));
  // Probe on rd
  // Probe on Write_Data
  Demultiplexer #(.enable("false"), .select(5), .width(32)) demultiplexer_1 (
    .out1(inx1), .out2(inx2), .out3(inx3), .out4(inx4), .out5(inx5), .out6(inx6), .out7(inx7), .out8(inx8),
    .out9(inx9), .out10(inx10), .out11(inx11), .out12(inx12), .out13(inx13), .out14(inx14), .out15(inx15),
    .out16(inx16), .out17(inx17), .out18(inx18), .out19(inx19), .out20(inx20), .out21(inx21), .out22(inx22),
    .out23(inx23), .out24(inx24), .out25(inx25), .out26(inx26), .out27(inx27), .out28(inx28), .out29(inx29),
    .out30(inx30), .out31(inx31), .in(Write_Data), .sel(rd));  // open: out0
  Register #(.width(32)) x9 (
    .D(regdatainput_9_data_out), .en(regdatainput_9_writeflag), .clk(clk), .Q(s1));  // open: clr
  regdatainput regdatainput_9 (
    .data_in(inx9), .write_en(RegWEn), .data_out(regdatainput_9_data_out),
    .writeflag(regdatainput_9_writeflag));
  Register #(.width(32)) x10 (
    .D(regdatainput_10_data_out), .en(regdatainput_10_writeflag), .clk(clk), .Q(a0));  // open: clr
  regdatainput regdatainput_10 (
    .data_in(inx10), .write_en(RegWEn), .data_out(regdatainput_10_data_out),
    .writeflag(regdatainput_10_writeflag));
  Register #(.width(32)) x11 (
    .D(regdatainput_11_data_out), .en(regdatainput_11_writeflag), .clk(clk), .Q(outx11));  // open: clr
  regdatainput regdatainput_11 (
    .data_in(inx11), .write_en(RegWEn), .data_out(regdatainput_11_data_out),
    .writeflag(regdatainput_11_writeflag));
  Register #(.width(32)) x12 (
    .D(regdatainput_12_data_out), .en(regdatainput_12_writeflag), .clk(clk), .Q(outx12));  // open: clr
  regdatainput regdatainput_12 (
    .data_in(inx12), .write_en(RegWEn), .data_out(regdatainput_12_data_out),
    .writeflag(regdatainput_12_writeflag));
  Register #(.width(32)) x13 (
    .D(regdatainput_13_data_out), .en(regdatainput_13_writeflag), .clk(clk), .Q(outx4));  // open: clr
  regdatainput regdatainput_13 (
    .data_in(inx4), .write_en(RegWEn), .data_out(regdatainput_13_data_out),
    .writeflag(regdatainput_13_writeflag));
  Register #(.width(32)) x14 (
    .D(regdatainput_14_data_out), .en(regdatainput_14_writeflag), .clk(clk), .Q(outx14));  // open: clr
  regdatainput regdatainput_14 (
    .data_in(inx14), .write_en(RegWEn), .data_out(regdatainput_14_data_out),
    .writeflag(regdatainput_14_writeflag));
  Register #(.width(32)) x15 (
    .D(regdatainput_15_data_out), .en(regdatainput_15_writeflag), .clk(clk), .Q(outx15));  // open: clr
  regdatainput regdatainput_15 (
    .data_in(inx15), .write_en(RegWEn), .data_out(regdatainput_15_data_out),
    .writeflag(regdatainput_15_writeflag));
  Register #(.width(32)) x16 (
    .D(regdatainput_16_data_out), .en(regdatainput_16_writeflag), .clk(clk), .Q(outx16));  // open: clr
  regdatainput regdatainput_16 (
    .data_in(inx16), .write_en(RegWEn), .data_out(regdatainput_16_data_out),
    .writeflag(regdatainput_16_writeflag));
  Register #(.width(32)) x17 (
    .D(regdatainput_17_data_out), .en(regdatainput_17_writeflag), .clk(clk), .Q(outx17));  // open: clr
  regdatainput regdatainput_17 (
    .data_in(inx17), .write_en(RegWEn), .data_out(regdatainput_17_data_out),
    .writeflag(regdatainput_17_writeflag));
  Register #(.width(32)) x18 (
    .D(regdatainput_18_data_out), .en(regdatainput_18_writeflag), .clk(clk), .Q(outx18));  // open: clr
  regdatainput regdatainput_18 (
    .data_in(inx18), .write_en(RegWEn), .data_out(regdatainput_18_data_out),
    .writeflag(regdatainput_18_writeflag));
  Register #(.width(32)) x19 (
    .D(regdatainput_19_data_out), .en(regdatainput_19_writeflag), .clk(clk), .Q(outx19));  // open: clr
  regdatainput regdatainput_19 (
    .data_in(inx19), .write_en(RegWEn), .data_out(regdatainput_19_data_out),
    .writeflag(regdatainput_19_writeflag));
  Register #(.width(32)) x20 (
    .D(regdatainput_20_data_out), .en(regdatainput_20_writeflag), .clk(clk), .Q(outx20));  // open: clr
  regdatainput regdatainput_20 (
    .data_in(inx20), .write_en(RegWEn), .data_out(regdatainput_20_data_out),
    .writeflag(regdatainput_20_writeflag));
  Register #(.width(32)) x21 (
    .D(regdatainput_21_data_out), .en(regdatainput_21_writeflag), .clk(clk), .Q(outx21));  // open: clr
  regdatainput regdatainput_21 (
    .data_in(inx21), .write_en(RegWEn), .data_out(regdatainput_21_data_out),
    .writeflag(regdatainput_21_writeflag));
  Register #(.width(32)) x22 (
    .D(regdatainput_22_data_out), .en(regdatainput_22_writeflag), .clk(clk), .Q(outx22));  // open: clr
  regdatainput regdatainput_22 (
    .data_in(inx22), .write_en(RegWEn), .data_out(regdatainput_22_data_out),
    .writeflag(regdatainput_22_writeflag));
  Register #(.width(32)) x23 (
    .D(regdatainput_23_data_out), .en(regdatainput_23_writeflag), .clk(clk), .Q(outx23));  // open: clr
  regdatainput regdatainput_23 (
    .data_in(inx23), .write_en(RegWEn), .data_out(regdatainput_23_data_out),
    .writeflag(regdatainput_23_writeflag));
  Register #(.width(32)) x24 (
    .D(regdatainput_24_data_out), .en(regdatainput_24_writeflag), .clk(clk), .Q(outx24));  // open: clr
  regdatainput regdatainput_24 (
    .data_in(inx24), .write_en(RegWEn), .data_out(regdatainput_24_data_out),
    .writeflag(regdatainput_24_writeflag));
  Multiplexer #(.enable("false"), .select(5), .width(32)) multiplexer_1 (
    .in0(outx0), .in1(ra), .in2(sp), .in3(outx3), .in4(outx4), .in5(t0), .in6(t1), .in7(t2), .in8(s0),
    .in9(s1), .in10(a0), .in11(outx11), .in12(outx12), .in13(outx13), .in14(outx14), .in15(outx15),
    .in16(outx16), .in17(outx17), .in18(outx18), .in19(outx19), .in20(outx20), .in21(outx21), .in22(outx22),
    .in23(outx23), .in24(outx24), .in25(outx25), .in26(outx26), .in27(outx27), .in28(outx28), .in29(outx29),
    .in30(outx30), .in31(outx31), .out(Read_Data_1), .sel(rs1));
  Register #(.width(32)) x25 (
    .D(regdatainput_25_data_out), .en(regdatainput_25_writeflag), .clk(clk), .Q(outx25));  // open: clr
  regdatainput regdatainput_25 (
    .data_in(inx25), .write_en(RegWEn), .data_out(regdatainput_25_data_out),
    .writeflag(regdatainput_25_writeflag));
  Register #(.width(32)) x26 (
    .D(regdatainput_26_data_out), .en(regdatainput_26_writeflag), .clk(clk), .Q(outx26));  // open: clr
  regdatainput regdatainput_26 (
    .data_in(inx26), .write_en(RegWEn), .data_out(regdatainput_26_data_out),
    .writeflag(regdatainput_26_writeflag));
  Register #(.width(32)) x27 (
    .D(regdatainput_27_data_out), .en(regdatainput_27_writeflag), .clk(clk), .Q(outx27));  // open: clr
  regdatainput regdatainput_27 (
    .data_in(inx27), .write_en(RegWEn), .data_out(regdatainput_27_data_out),
    .writeflag(regdatainput_27_writeflag));
  Register #(.width(32)) x28 (
    .D(regdatainput_28_data_out), .en(regdatainput_28_writeflag), .clk(clk), .Q(outx28));  // open: clr
  regdatainput regdatainput_28 (
    .data_in(inx28), .write_en(RegWEn), .data_out(regdatainput_28_data_out),
    .writeflag(regdatainput_28_writeflag));
  Register #(.width(32)) x29 (
    .D(regdatainput_29_data_out), .en(regdatainput_29_writeflag), .clk(clk), .Q(outx29));  // open: clr
  regdatainput regdatainput_29 (
    .data_in(inx29), .write_en(RegWEn), .data_out(regdatainput_29_data_out),
    .writeflag(regdatainput_29_writeflag));
  Register #(.width(32)) x30 (
    .D(regdatainput_30_data_out), .en(regdatainput_30_writeflag), .clk(clk), .Q(outx30));  // open: clr
  regdatainput regdatainput_30 (
    .data_in(inx30), .write_en(RegWEn), .data_out(regdatainput_30_data_out),
    .writeflag(regdatainput_30_writeflag));
  Register #(.width(32)) x31 (
    .D(regdatainput_31_data_out), .en(regdatainput_31_writeflag), .clk(clk), .Q(outx31));  // open: clr
  regdatainput regdatainput_31 (
    .data_in(inx31), .write_en(RegWEn), .data_out(regdatainput_31_data_out),
    .writeflag(regdatainput_31_writeflag));
  Multiplexer #(.enable("false"), .select(5), .width(32)) multiplexer_2 (
    .in0(outx0), .in1(ra), .in2(sp), .in3(outx3), .in4(outx4), .in5(t0), .in6(t1), .in7(t2), .in8(s0),
    .in9(s1), .in10(a0), .in11(outx11), .in12(outx12), .in13(outx13), .in14(outx14), .in15(outx15),
    .in16(outx16), .in17(outx17), .in18(outx18), .in19(outx19), .in20(outx20), .in21(outx21), .in22(outx22),
    .in23(outx23), .in24(outx24), .in25(outx25), .in26(outx26), .in27(outx27), .in28(outx28), .in29(outx29),
    .in30(outx30), .in31(outx31), .out(Read_Data_2), .sel(rs2));

  // Other names for the same wires on the sheet: outx1[31:0] = ra; outx2[31:0] = sp; outx5[31:0] = t0;
  //   outx6[31:0] = t1; outx7[31:0] = t2; outx8[31:0] = s0; outx9[31:0] = s1; outx10[31:0] = a0;
  //   read_data1[31:0] = Read_Data_1; read_data2[31:0] = Read_Data_2; read_reg1[4:0] = rs1; read_reg2[4:0] = rs2;
  //   write_en = RegWEn; write_reg[4:0] = rd

  // Notes on the sheet:
  //   INPUTS to your circuit
  //   DON'T CHANGE THE LOCATIONS OF THE INPUTS AND OUTPUTS!
  //   These are DEBUG/TEST outputs from your circuit.
  //   OUTPUTS from your circuit
endmodule

module regdatainput (
  input  [31:0] data_in,
  input  write_en,
  output [31:0] data_out,
  output writeflag
);

  wire or_1_out, or_2_out, or_3_out, or_4_out, or_5_out, or_6_out, or_7_out, or_8_out, or_9_out, or_10_out,
       or_11_out, or_12_out, or_13_out, or_14_out, or_15_out, or_16_out, or_17_out, or_18_out, or_19_out,
       or_20_out, or_21_out, or_22_out, or_23_out, or_24_out, or_25_out, or_26_out, or_27_out, or_28_out,
       or_29_out, or_30_out, or_31_out;

  or or_1 (or_1_out, data_in[31], data_in[30]);
  or or_2 (or_2_out, data_in[29], data_in[28]);
  or or_3 (or_3_out, or_1_out, or_2_out);
  or or_4 (or_4_out, data_in[27], data_in[26]);
  or or_5 (or_5_out, data_in[25], data_in[24]);
  or or_6 (or_6_out, or_4_out, or_5_out);
  or or_7 (or_7_out, or_3_out, or_6_out);
  or or_8 (or_8_out, data_in[23], data_in[22]);
  or or_9 (or_9_out, data_in[21], data_in[20]);
  or or_10 (or_10_out, or_8_out, or_9_out);
  or or_11 (or_11_out, or_7_out, or_15_out);
  or or_12 (or_12_out, data_in[19], data_in[18]);
  or or_13 (or_13_out, data_in[17], data_in[16]);
  or or_14 (or_14_out, or_12_out, or_13_out);
  or or_15 (or_15_out, or_10_out, or_14_out);
  or or_16 (or_16_out, data_in[15], data_in[14]);
  or or_17 (or_17_out, data_in[13], data_in[12]);
  or or_18 (or_18_out, or_16_out, or_17_out);
  or or_19 (or_19_out, or_11_out, or_27_out);
  or or_20 (or_20_out, data_in[11], data_in[10]);
  or or_21 (or_21_out, data_in[9], data_in[8]);
  or or_22 (or_22_out, or_20_out, or_21_out);
  or or_23 (or_23_out, or_18_out, or_22_out);
  and and_1 (writeflag, or_19_out, write_en);
  or or_24 (or_24_out, data_in[7], data_in[6]);
  or or_25 (or_25_out, data_in[5], data_in[4]);
  or or_26 (or_26_out, or_24_out, or_25_out);
  or or_27 (or_27_out, or_23_out, or_31_out);
  or or_28 (or_28_out, data_in[3], data_in[2]);
  or or_29 (or_29_out, data_in[1], data_in[0]);
  or or_30 (or_30_out, or_28_out, or_29_out);
  or or_31 (or_31_out, or_26_out, or_30_out);

  assign data_out = data_in;
endmodule
