// Logisim project cpu-branch_jump.circ as structural Verilog: 1 circuit, main circuit run_main
module run_main (
  output [31:0] ra,
  output [31:0] sp,
  output [31:0] t0,
  output [31:0] t1,
  output [31:0] t2,
  output [31:0] s0,
  output [31:0] s1,
  output [31:0] a0,
  output [31:0] Requested_Address,
  output [31:0] Requested_Instruction,
  output [15:0] Time_Step,
  output halt
);

  wire clk;

  Clock clock_1 (.out(clk));
  // Probe on Requested_Address
  // test_harness test_harness_1: pin names not known; wires that end beside it: Requested_Instruction, clk, Requested_Address, ra, sp, t0, t1, t2, s0, s1, a0
  ROM #(.addrWidth(14), .dataWidth(32)) rom_1 (.addr(Requested_Address[15:2]), .data(Requested_Instruction));
  // Probe on Requested_Instruction
  Counter #(.max('hffff), .width(16)) counter_1 (.clk(clk), .Q(Time_Step));  // open: clr, load, up, count, D, carry
  Comparator #(.width(16)) comparator_1 (.a(Time_Step), .b(16'h44), .eq(halt));  // open: gt, lt

  // Other names for the same wires on the sheet: fetch_addr[31:0] = Requested_Address;
  //   Instruction[31:0] = Requested_Instruction

  // Notes on the sheet:
  //   contents of rom_1 (hex, n*v repeats v):
  //   00A00093 00A00113 00208663 003181B3 0140006F 002081B3 00A00193 00500213 FE4186E3 00000033 00A00093
  //   00500113 00209463 00208093 01F08093 00A00193 00A00213 FE4198E3 FFF00093 00500113 0020C463 00208093
  //   01F08093 00A00193 00A00213 FE41C8E3 06400193 00A00213 FE41C2E3 00A00093 00500113 0020D463 00208093
  //   01E08093 00300193 00500213 FE41D8E3 00A00093 00A00113 0020D463 00208093 01E08093 00000513 FFF00093
  //   80000137 FFF10113 0020EC63 00100193 80000237 00020213 0041E663 00C0006F 00200513 00100513 00000513
  //   800000B7 00008093 80000137 FFF10113 0020F463 01C0006F 00100513 00100193 FFF00213 0041F463 0031F463
  //   00200513
  //   Instruction Memory
  //   Halts Execution After Constant # of Clock Cycles
  //   Constant
endmodule
