// Logisim project control_logic.circ as structural Verilog: 1 circuit, main circuit control_logic
module control_logic (
  input  [31:0] inst,
  input  BrEq,
  input  BrLt,
  output PCSel,
  output RegWEn,
  output [2:0] ImmSel,
  output BrUn,
  output ASel,
  output BSel,
  output [3:0] ALUSel,
  output MemRW,
  output [1:0] WBSel,
  output CSRSel,
  output CSRWen
);

  wire and_1_out, and_2_out, auipc, branch, handles_srli_vs_srlai_out, jump, load, lui, math, not_1_out,
       not_2_out, not_3_out, store;
  wire [2:0] Imm_Reg_Ops_data, multiplexer_1_out, multiplexer_2_out;
  wire [14:0] Control_LOGIC_data;

  Demultiplexer #(.enable("false"), .select(3)) demultiplexer_1 (
    .out0(load), .out1(branch), .out2(BSel), .out3(auipc), .out4(store), .out5(jump), .out6(math),
    .out7(lui), .in(1'b1), .sel(multiplexer_1_out));
  and and_1 (and_1_out, inst[6], not_1_out);
  not not_1 (not_1_out, inst[2]);
  ROM #(.addrWidth(11), .dataWidth(15)) Control_LOGIC (.data(Control_LOGIC_data));  // open: addr
  Multiplexer #(.enable("false"), .width(3)) multiplexer_1 (
    .in0({inst[5:4], inst[2]}), .in1(3'b001), .out(multiplexer_1_out), .sel(and_1_out));
  Multiplexer #(.enable("false"), .width(3)) multiplexer_2 (
    .in0(inst[14:12]), .in1(3'b011), .out(multiplexer_2_out), .sel(handles_srli_vs_srlai_out));
  and handles_srli_vs_srlai (handles_srli_vs_srlai_out, and_2_out, inst[5]);
  and and_2 (and_2_out, inst[14], not_2_out);
  not not_2 (not_2_out, inst[13]);
  ROM #(.addrWidth(3), .dataWidth(3)) Imm_Reg_Ops (.addr(multiplexer_2_out), .data(Imm_Reg_Ops_data));
  not not_3 (not_3_out, BSel);
  not not_4 (ASel, BSel);
  not not_5 (PCSel, BSel);
  assign ImmSel = {{2{1'b0}}, not_3_out};  // Bit_Extender bit_extender_1
  not not_6 (MemRW, BSel);
  assign WBSel = {{1{1'b0}}, BSel};  // Bit_Extender bit_extender_2
  assign ALUSel = {{1{1'b0}}, Imm_Reg_Ops_data};  // Bit_Extender bit_extender_3

  assign RegWEn = BSel;

  // Other names for the same wires on the sheet: sign = inst[30]; func3[2:0] = inst[14:12]; opcode[4:0] = inst[6:2];
  //   imm_reg = BSel

  // Notes on the sheet:
  //   contents of Control_LOGIC (hex, n*v repeats v):
  //   15*0 2081
  //   INPUTS to your circuit
  //   DON'T CHANGE THE LOCATIONS OF THE INPUTS AND OUTPUTS!
  //   OUTPUT from your circuit
  //   contents of Imm_Reg_Ops (hex, n*v repeats v):
  //   0 6 7 5 3 4 2 1
endmodule
